# Fritzing sketch SnowMagic_WithStepper (saved by Fritzing 1.0.7)
breadboards: 1

parts:
  A1 = Arduino R4 Minima
  Step_Control = TB6600 v1.2 module
  Pitch = linear actuator [package=THT]
  IMU = Adafruit ICM20948
  U1 = JOYSTICK-PSP1000 [package=joystick-psp1000]
  Stepper = Stepper Motor - Bipolar
  V1 = DC Power [voltage=20V internal_resistance=0.1Ω]
  GND = Camdenboss CTB0158-11 [part_number=GND package=THT]
  20_VDC = Camdenboss CTB0158-11 [part_number=VDC package=THT]
  5_VDC = Camdenboss CTB0158-11 [part_number=VDC package=THT]
  R1 = Resistor [tolerance=±5% power=0.25W resistance=47k package=THT]
  12k_Ohms = Resistor [tolerance=±5% power=0.25W resistance=10k package=THT]
  Deadman = Pushbutton [package=THT]
  Joystick_Button = Pushbutton [package=THT]
  RGB = RGB LED (com. cathode, rgb) [color="Red (633nm)" current=0.030A package="5 mm [THT]"]
  R2 = Resistor [tolerance=±5% power=0.25W resistance=100 package=THT]
  R3 = Resistor [tolerance=±5% power=0.25W resistance=100 package=THT]
  R4 = Resistor [tolerance=±5% power=0.25W resistance=220 package=THT]
  MD10C = MD10C R2
  S2 = Pushbutton [package=THT]
  S1 = Pushbutton [package=THT]

nets:
  N1: A1.Pin_5, 5_VDC.terminal_11
  N2: A1.Pin_6, A1.Pin_7, A1.Pin_17, A1.Pin_45, GND.pin11
  N3: A1.Pin_8, 20_VDC.pin10
  N4: A1.Pin_9, R1.Pin_1, 12k_Ohms.Pin_0
  N5: A1.Pin_10, U1.Y
  N6: A1.Pin_11, U1.X
  N7: A1.Pin_33, S1.leg1
  N8: A1.Pin_34, S2.leg1
  N9: A1.Pin_35, Step_Control.Pin_3
  N10: A1.Pin_36, Step_Control.Pin_2
  N11: A1.Pin_37, MD10C.no_name_yet#connector_1
  N12: A1.Pin_38, MD10C.no_name_yet#connector_2
  N13: A1.Pin_39, Joystick_Button.leg0
  N14: A1.Pin_40, R2.Pin_1
  N15: A1.Pin_41, R3.Pin_1
  N16: A1.Pin_42, R4.Pin_1
  N17: A1.Pin_47, IMU.SDI/SDA
  N18: A1.Pin_48, IMU.SCK/SCL
  N19: Step_Control.Pin_1, Step_Control.Pin_4, 5_VDC.pin10
  N20: Step_Control.Pin_9, 20_VDC.pin9
  N21: Step_Control.Pin_10, GND.pin6
  N22: Step_Control.Pin_11, Stepper.D
  N23: Step_Control.Pin_12, Stepper.B
  N24: Step_Control.Pin_13, Stepper.C
  N25: Step_Control.Pin_14, Stepper.A
  N26: Pitch.pin1, MD10C.no_name_yet#connectorB-4
  N27: Pitch.pin2, MD10C.no_name_yet#connectorA-3
  N28: IMU.GND, GND.pin1
  N29: IMU.VIN, 5_VDC.pin1
  N30: U1.GND, GND.pin7, Joystick_Button.leg1
  N31: U1.VCC, 5_VDC.pin11
  N32: V1.V-, GND.terminal_11
  N33: V1.V+, Deadman.leg1
  N34: GND.pin2, RGB.common_cathode
  N35: GND.pin3, MD10C.no_name_yet#connector_3, MD10C.no_name_yet#connectornegative-2
  N36: GND.pin8, S2.leg0
  N37: GND.pin9, S1.leg0
  N38: GND.pin10, 12k_Ohms.Pin_1
  N39: 20_VDC.pin8, MD10C.no_name_yet#connectorpositive-1
  N40: 20_VDC.pin11, R1.Pin_0
  N41: 20_VDC.terminal_11, Deadman.leg0
  N42: RGB.red_anode, R4.Pin_0
  N43: RGB.green_anode, R3.Pin_0
  N44: RGB.blue_anode, R2.Pin_0

custom parts:
  Arduino R4 Minima: Introducing the Arduino UNO R4 Minima! This board boasts the RA4M1 microprocessor from Renesas, delivering increased processing power, expanded memory, and additional peripherals.
  TB6600 v1.2 module: 24-32V 4.5A 2Phase Stepper Motor Driver BL-TB6600-V1.2.
  linear actuator: Generic linear actuator.
